// Logisim project Cwiczenia07.circ as structural Verilog
module Zadanie2 (
  input  a,
  input  b,
  input  c,
  output y
);

  wire and_1_out, not_1_out, xor_1_out;

  not not_1 (not_1_out, b);
  xor xor_1 (xor_1_out, a, b);
  and and_1 (and_1_out, a, not_1_out, c);
  or or_1 (y, xor_1_out, and_1_out, c);
endmodule

module NOT (
  input  a,
  output y
);

  nand nand_1 (y, a, a);
endmodule

module AND (
  input  a,
  input  b,
  output out_3
);

  wire nand_1_out;

  nand nand_1 (nand_1_out, a, b);
  nand nand_2 (out_3, nand_1_out, nand_1_out);
endmodule

module OR (
  input  a,
  input  b,
  output y
);

  wire nand_1_out, nand_2_out;

  nand nand_1 (nand_1_out, a, a);
  nand nand_2 (nand_2_out, b, b);
  nand nand_3 (y, nand_1_out, nand_2_out);
endmodule

module Zadanie4 (
  input  a,
  input  b,
  input  c,
  output y
);

  wire and_1_out_3, and_2_out_3, and_3_out_3, and_4_out_3, not_1_y, not_2_y, or_1_y, or_2_y;

  NOT not_1 (.a(b), .y(not_1_y));
  NOT not_2 (.a(a), .y(not_2_y));
  AND and_1 (.a(a), .b(b), .out_3(and_1_out_3));
  AND and_2 (.a(not_2_y), .b(b), .out_3(and_2_out_3));
  OR or_1 (.a(and_2_out_3), .b(and_3_out_3), .y(or_1_y));
  AND and_3 (.a(a), .b(not_1_y), .out_3(and_3_out_3));
  AND and_4 (.a(and_1_out_3), .b(c), .out_3(and_4_out_3));
  OR or_2 (.a(or_1_y), .b(and_4_out_3), .y(or_2_y));
  OR or_3 (.a(or_2_y), .b(c), .y(y));
endmodule
