// Logisim project Cwiczenia08.circ as structural Verilog
module Zadanie2 (
  input  a,
  input  b,
  input  c,
  output y
);

  wire and_1_out, not_1_out, xor_1_out;

  not not_1 (not_1_out, b);
  xor xor_1 (xor_1_out, a, b);
  and and_1 (and_1_out, a, not_1_out, c);
  or or_1 (y, xor_1_out, and_1_out, c);
endmodule

module NOT (
  input  a,
  output y
);

  nand nand_1 (y, a, a);
endmodule

module AND (
  input  a,
  input  b,
  output out_3
);

  wire nand_1_out;

  nand nand_1 (nand_1_out, a, b);
  nand nand_2 (out_3, nand_1_out, nand_1_out);
endmodule

module OR (
  input  a,
  input  b,
  output y
);

  wire nand_1_out, nand_2_out;

  nand nand_1 (nand_1_out, a, a);
  nand nand_2 (nand_2_out, b, b);
  nand nand_3 (y, nand_1_out, nand_2_out);
endmodule

module Zadanie4 (
  input  a,
  input  b,
  input  c,
  output y
);

  wire and_1_out_3, and_2_out_3, and_3_out_3, and_4_out_3, not_1_y, not_2_y, or_1_y, or_2_y;

  NOT not_1 (.a(b), .y(not_1_y));
  NOT not_2 (.a(a), .y(not_2_y));
  AND and_1 (.a(a), .b(b), .out_3(and_1_out_3));
  AND and_2 (.a(not_2_y), .b(b), .out_3(and_2_out_3));
  OR or_1 (.a(and_2_out_3), .b(and_3_out_3), .y(or_1_y));
  AND and_3 (.a(a), .b(not_1_y), .out_3(and_3_out_3));
  AND and_4 (.a(and_1_out_3), .b(c), .out_3(and_4_out_3));
  OR or_2 (.a(or_1_y), .b(and_4_out_3), .y(or_2_y));
  OR or_3 (.a(or_2_y), .b(c), .y(y));
endmodule

module LAB008_Zadanie1 (
  input  in_1,
  input  in_2,
  input  in_3,
  input  in_4,
  output y
);

  wire and_1_out, and_2_out, and_3_out, and_4_out, not_1_out, not_2_out, not_3_out, not_4_out;

  not not_1 (not_1_out, in_1);
  not not_2 (not_2_out, in_2);
  not not_3 (not_3_out, in_3);
  not not_4 (not_4_out, in_4);
  and and_1 (and_1_out, not_1_out, not_2_out, not_3_out, in_4);
  and and_2 (and_2_out, not_1_out, not_2_out, in_3, in_4);
  and and_3 (and_3_out, not_1_out, in_2, in_3, in_4);
  and and_4 (and_4_out, in_1, in_2, not_3_out, not_4_out);
  or or_1 (y, and_1_out, and_2_out, and_3_out, and_4_out);
endmodule

module LAB008_Zadanie1_NANDS (
  input  a,
  input  b,
  input  c,
  input  d,
  output y
);

  wire and_1_out_3, and_2_out_3, and_3_out_3, and_4_out_3, and_5_out_3, and_6_out_3, and_7_out_3,
       and_8_out_3, and_9_out_3, and_10_out_3, and_11_out_3, and_12_out_3, not_1_y, not_2_y, not_3_y,
       not_4_y, or_1_y, or_2_y;

  NOT not_1 (.a(a), .y(not_1_y));
  NOT not_2 (.a(b), .y(not_2_y));
  NOT not_3 (.a(c), .y(not_3_y));
  NOT not_4 (.a(d), .y(not_4_y));
  AND and_1 (.a(not_1_y), .b(not_2_y), .out_3(and_1_out_3));
  AND and_2 (.a(and_1_out_3), .b(not_3_y), .out_3(and_2_out_3));
  AND and_3 (.a(not_1_y), .b(not_2_y), .out_3(and_3_out_3));
  AND and_4 (.a(and_3_out_3), .b(c), .out_3(and_4_out_3));
  AND and_5 (.a(not_1_y), .b(b), .out_3(and_5_out_3));
  AND and_6 (.a(and_5_out_3), .b(c), .out_3(and_6_out_3));
  AND and_7 (.a(a), .b(b), .out_3(and_7_out_3));
  AND and_8 (.a(and_7_out_3), .b(not_3_y), .out_3(and_8_out_3));
  AND and_9 (.a(and_2_out_3), .b(d), .out_3(and_9_out_3));
  AND and_10 (.a(and_4_out_3), .b(d), .out_3(and_10_out_3));
  AND and_11 (.a(and_6_out_3), .b(d), .out_3(and_11_out_3));
  AND and_12 (.a(and_8_out_3), .b(not_4_y), .out_3(and_12_out_3));
  OR or_1 (.a(and_9_out_3), .b(and_10_out_3), .y(or_1_y));
  OR or_2 (.a(or_1_y), .b(and_11_out_3), .y(or_2_y));
  OR or_3 (.a(or_2_y), .b(and_12_out_3), .y(y));
endmodule

module LAB008_Zadanie2 (
  input  LC,
  input  SC,
  input  PC,
  output LK,
  output PK
);

  wire and_1_out, not_1_out, not_2_out, not_3_out, not_4_out;

  not not_1 (not_1_out, SC);
  not not_2 (not_2_out, PC);
  not not_3 (not_3_out, LC);
  or or_1 (LK, not_1_out, not_2_out);
  not not_4 (not_4_out, SC);
  and and_1 (and_1_out, not_3_out, PC);
  or or_2 (PK, not_4_out, and_1_out);
endmodule

// NOT
module NOT_NOR (
  input  a,
  output y
);

  nor nor_1 (y, a, a);
endmodule

// AND
module AND_NOR (
  input  a,
  input  b,
  output y
);

  wire nor_1_out, nor_2_out;

  nor nor_1 (nor_1_out, a, a);
  nor nor_2 (nor_2_out, b, b);
  nor nor_3 (y, nor_1_out, nor_2_out);
endmodule

// OR
module OR_NOR (
  input  a,
  input  b,
  output y
);

  wire nor_1_out;

  nor nor_1 (nor_1_out, a, b);
  nor nor_2 (y, nor_1_out, nor_1_out);
endmodule

module LAB008_Zadanie2_NORS (
  input  LC,
  input  SC,
  input  PC,
  output LK,
  output PK
);

  wire and_nor_1_y, not_nor_1_y, not_nor_2_y, not_nor_3_y, not_nor_4_y;

  NOT_NOR not_nor_1 (.a(SC), .y(not_nor_1_y));
  NOT_NOR not_nor_2 (.a(PC), .y(not_nor_2_y));
  NOT_NOR not_nor_3 (.a(LC), .y(not_nor_3_y));
  OR_NOR or_nor_1 (.a(not_nor_1_y), .b(not_nor_2_y), .y(LK));
  NOT_NOR not_nor_4 (.a(SC), .y(not_nor_4_y));
  AND_NOR and_nor_1 (.a(not_nor_3_y), .b(PC), .y(and_nor_1_y));
  OR_NOR or_nor_2 (.a(not_nor_4_y), .b(and_nor_1_y), .y(PK));
endmodule
