// Logisim project Zadania.circ as structural Verilog
module Zadanie01 (
  input  in_1,
  input  in_2,
  output out_3
);

  wire clock_1_out, d_ff_1_q, d_ff_2_q, d_ff_3_q;

  D_Flip_Flop d_ff_1 (.D(in_1), .clk(clock_1_out), .Q(d_ff_1_q), .reset(in_2));  // open: Qn, preset
  Clock clock_1 (.out(clock_1_out));
  D_Flip_Flop d_ff_2 (.D(d_ff_1_q), .clk(clock_1_out), .Q(d_ff_2_q), .reset(in_2));  // open: Qn, preset
  D_Flip_Flop d_ff_3 (.D(d_ff_2_q), .clk(clock_1_out), .Q(d_ff_3_q), .reset(in_2));  // open: Qn, preset
  D_Flip_Flop d_ff_4 (.D(d_ff_3_q), .clk(clock_1_out), .Q(out_3), .reset(in_2));  // open: Qn, preset
endmodule

module Zadanie02 (
  input  in_1,
  output out_2,
  output out_3,
  output out_4,
  output out_5
);

  wire clock_1_out;

  D_Flip_Flop d_ff_1 (.D(out_5), .clk(clock_1_out), .Q(out_2), .preset(in_1));  // open: Qn, reset
  Clock clock_1 (.out(clock_1_out));
  D_Flip_Flop d_ff_2 (.D(out_2), .clk(clock_1_out), .Q(out_3), .reset(in_1));  // open: Qn, preset
  D_Flip_Flop d_ff_3 (.D(out_3), .clk(clock_1_out), .Q(out_4), .reset(in_1));  // open: Qn, preset
  D_Flip_Flop d_ff_4 (.D(out_4), .clk(clock_1_out), .Q(out_5), .reset(in_1));  // open: Qn, preset
endmodule

module Zadanie03 (
  output out_1,
  output out_2,
  output out_3,
  output out_4,
  output out_5
);

  wire clock_1_out, d_ff_4_qn;

  Clock clock_1 (.out(clock_1_out));
  D_Flip_Flop d_ff_1 (.D(d_ff_4_qn), .clk(clock_1_out), .Q(out_1));  // open: Qn, preset, reset
  D_Flip_Flop d_ff_2 (.D(out_1), .clk(clock_1_out), .Q(out_2));  // open: Qn, preset, reset
  D_Flip_Flop d_ff_3 (.D(out_2), .clk(clock_1_out), .Q(out_4));  // open: Qn, preset, reset
  D_Flip_Flop d_ff_4 (.D(out_4), .clk(clock_1_out), .Q(out_5), .Qn(d_ff_4_qn));  // open: preset, reset

  assign out_3 = out_2;
endmodule

module Zadanie04 (
  output out_1,
  output out_2,
  output out_3,
  output out_4
);

  wire and_1_out, clock_1_out, d_ff_1_qn, d_ff_2_qn, d_ff_3_qn, d_ff_4_qn;

  D_Flip_Flop d_ff_1 (.D(d_ff_1_qn), .clk(clock_1_out), .Q(out_1), .Qn(d_ff_1_qn), .reset(and_1_out));  // open: preset
  Clock clock_1 (.out(clock_1_out));
  D_Flip_Flop d_ff_2 (.D(d_ff_2_qn), .clk(d_ff_1_qn), .Q(out_2), .Qn(d_ff_2_qn), .reset(and_1_out));  // open: preset
  D_Flip_Flop d_ff_3 (.D(d_ff_3_qn), .clk(d_ff_2_qn), .Q(out_3), .Qn(d_ff_3_qn), .reset(and_1_out));  // open: preset
  D_Flip_Flop d_ff_4 (.D(d_ff_4_qn), .clk(d_ff_3_qn), .Q(out_4), .Qn(d_ff_4_qn), .reset(and_1_out));  // open: preset
  and and_1 (and_1_out, out_1, out_4);
endmodule

module Zadanie05 (
  output out_1,
  output out_2,
  output out_3,
  output out_4
);

  wire and_1_out, clock_1_out, d_ff_1_qn, d_ff_2_qn, d_ff_3_qn, d_ff_4_qn;

  D_Flip_Flop d_ff_1 (.D(d_ff_1_qn), .clk(clock_1_out), .Q(out_1), .Qn(d_ff_1_qn), .preset(and_1_out));  // open: reset
  Clock clock_1 (.out(clock_1_out));
  D_Flip_Flop d_ff_2 (.D(d_ff_2_qn), .clk(d_ff_1_qn), .Q(out_2), .Qn(d_ff_2_qn), .preset(and_1_out));  // open: reset
  D_Flip_Flop d_ff_3 (.D(d_ff_3_qn), .clk(d_ff_2_qn), .Q(out_3), .Qn(d_ff_3_qn), .reset(and_1_out));  // open: preset
  D_Flip_Flop d_ff_4 (.D(d_ff_4_qn), .clk(d_ff_3_qn), .Q(out_4), .Qn(d_ff_4_qn), .reset(and_1_out));  // open: preset
  and and_1 (and_1_out, out_2, out_4);
endmodule

module Zadanie06 (
  output out_1,
  output out_2,
  output out_3,
  output out_4
);

  wire clock_1_out, xor_1_out;

  Clock clock_1 (.out(clock_1_out));
  D_Flip_Flop d_ff_1 (.D(xor_1_out), .clk(clock_1_out), .Q(out_1));  // open: Qn, preset, reset
  D_Flip_Flop d_ff_2 (.D(out_1), .clk(clock_1_out), .Q(out_2));  // open: Qn, preset, reset
  xor xor_1 (xor_1_out, out_4, out_3);
  D_Flip_Flop d_ff_3 (.D(out_2), .clk(clock_1_out), .Q(out_3));  // open: Qn, preset, reset
  D_Flip_Flop d_ff_4 (.D(out_3), .clk(clock_1_out), .Q(out_4));  // open: Qn, preset, reset
endmodule

module Zadanie07 (
  input  a,
  input  blokada,
  output y
);

  wire nand_1_out, nand_2_out, nand_4_out;

  nand nand_1 (nand_1_out, a, blokada);
  nand nand_2 (nand_2_out, blokada, ~a);  // NAND_Gate
  nand nand_3 (y, nand_1_out, nand_4_out);
  nand nand_4 (nand_4_out, y, nand_2_out);
endmodule

module Zadanie08 (
  input  in_1,
  output out_2,
  output out_3,
  output out_4,
  output out_5
);

  wire clock_1_out, d_ff_1_q, d_ff_2_q, d_ff_3_q, d_ff_4_q, d_ff_4_qn;

  Clock clock_1 (.out(clock_1_out));
  D_Flip_Flop d_ff_1 (.D(d_ff_4_qn), .clk(clock_1_out), .Q(d_ff_1_q));  // open: Qn, preset, reset
  Zadanie07 zadanie07_1 (.a(d_ff_1_q), .blokada(in_1), .y(out_2));
  D_Flip_Flop d_ff_2 (.D(d_ff_1_q), .clk(clock_1_out), .Q(d_ff_2_q));  // open: Qn, preset, reset
  Zadanie07 zadanie07_2 (.a(d_ff_2_q), .blokada(in_1), .y(out_3));
  D_Flip_Flop d_ff_3 (.D(d_ff_2_q), .clk(clock_1_out), .Q(d_ff_3_q));  // open: Qn, preset, reset
  Zadanie07 zadanie07_3 (.a(d_ff_3_q), .blokada(in_1), .y(out_4));
  D_Flip_Flop d_ff_4 (.D(d_ff_3_q), .clk(clock_1_out), .Q(d_ff_4_q), .Qn(d_ff_4_qn));  // open: preset, reset
  Zadanie07 zadanie07_4 (.a(d_ff_4_q), .blokada(in_1), .y(out_5));
endmodule
